// Logisim project DEM Project.circ as structural Verilog: 1 circuit, main circuit main
module main (
  input  in_1
);

  wire Access_ROM_data_out, Clear_RAM_out, Clear_Screen_out, Clock_out, controlled_buffer_1_out,
       controlled_buffer_2_out, keyboard_1_avail, Manual_Buffer_dump_out, Random_Character_Generator_out;
  wire [3:0] counter_1_q, counter_2_q;
  wire [6:0] keyboard_1_data, multiplexer_1_out, multiplexer_2_out, ram_1_data, random_1_out, rom_1_data;

  Clock Clock (.out(Clock_out));
  Counter #(.width(4), .max('hf)) counter_1 (
    .Q(counter_1_q), .clk(Clock_out), .clr(in_1));  // open: load, D, count, carry
  Multiplexer #(.width(7)) multiplexer_1 (
    .in0(multiplexer_2_out), .in1(ram_1_data), .out(multiplexer_1_out), .sel(Random_Character_Generator_out));  // open: en
  TTY tty_1 (.data(multiplexer_1_out), .clk(Clock_out), .clr(Clear_Screen_out));  // open: we
  Counter #(.width(4), .max('hf)) counter_2 (
    .Q(counter_2_q), .clk(controlled_buffer_1_out), .clr(Clear_RAM_out));  // open: load, D, count, carry
  assign controlled_buffer_1_out = 1'b1 ? Clock_out : 1'bz;  // Controlled_Buffer controlled_buffer_1
  Random #(.width(7)) random_1 (.clk(Clock_out), .out(random_1_out));  // open: next, clr
  ROM #(.addrWidth(4), .dataWidth(7)) rom_1 (.addr(counter_1_q), .data(rom_1_data));  // open: sel
  RAM #(.addrWidth(4), .dataWidth(7), .bus("separate")) ram_1 (
    .addr(counter_2_q), .din(random_1_out), .data(ram_1_data), .clk(controlled_buffer_1_out),
    .clr(Clear_RAM_out));  // open: str, sel, ld
  Multiplexer #(.width(7)) multiplexer_2 (
    .in0(keyboard_1_data), .in1(rom_1_data), .out(multiplexer_2_out), .sel(Access_ROM_data_out), .en(1'b1));
  assign controlled_buffer_2_out = keyboard_1_avail ? Clock_out : 1'bz;  // Controlled_Buffer controlled_buffer_2
  Keyboard keyboard_1 (
    .clk(controlled_buffer_2_out), .clr(Manual_Buffer_dump_out), .avail(keyboard_1_avail),
    .data(keyboard_1_data));  // open: re
  Button Access_ROM_data (.out(Access_ROM_data_out));
  Button Clear_Screen (.out(Clear_Screen_out));
  Button Random_Character_Generator (.out(Random_Character_Generator_out));
  Button Clear_RAM (.out(Clear_RAM_out));
  Button Manual_Buffer_dump (.out(Manual_Buffer_dump_out));

  // Notes on the sheet:
  //   ROM
  //   contents of rom_1 (hex, n*v repeats v):
  //   63 1 34 4 3 1 41 5 32 46 4 3 2 1 24 3
  //   RAM
  //   SCREEN
  //   Random Character Generator
  //   Controlled Buffer
  //   Custom Input
  //   Keyboard 
endmodule
